# Fritzing sketch project (saved by Fritzing 0.9.3b)
breadboards: 1

parts:
  PCB2 = RTC_DS1302_module
  Part1 = Arduino Uno (Rev3)
  Part2 = HX711 Weighing Sensor Module
  microSD1 = MicroSD Card Module
  Load_Cell1 = Load Cell - Red/white/black/green
  R4 = 100k0 Ω Resistor [package=THT]
  U1 = Sharp PC817 [package=THT]
  U2 = RELAY [package=relay-jzc]
  VCC1 = Battery  # not connected
  L1 = Inductor [package="400 mil [THT]"]  # not connected
  R5 = Resistor [tolerance=±5% resistance=220 package=THT]
  LED1 = DUO LED RG [package="5 mm [THT]"]
  R6 = 100k0 Ω Resistor [package=THT]
  S3 = Ignition [package="[THT]"]
  S4 = E-Stop [package="[THT]"]
  VCC2 = 12V Battery

nets:
  VCC: PCB2.VCC, Part2.VCC, microSD1.VCC, U2.COIL1, VCC2.+
  GND: PCB2.GND, Part2.GND, microSD1.GND, U1.Pin_2, U1.Pin_3, R5.Pin_0, S3.Pin_1, S3.Pin_2, S4.Pin_3, S4.Pin_4, VCC2.-
  N1: PCB2.RST, Part1.D5_PWM
  N2: PCB2.DAT, Part1.D2
  N3: PCB2.CLK, Part1.D8
  N4: Part1.D9_PWM, U1.Pin_1
  N5: Part1.D10_PWM/SS, LED1.red_anode
  N6: Part1.D11_PWM/MOSI, microSD1.MOSI
  N7: Part1.D12/MISO, microSD1.MISO
  N8: Part1.D13/SCK, microSD1.SCK
  N9: Part1.D0/RX, LED1.green_anode
  N10: Part1.D1/TX, R6.Pin_1
  N11: Part1.D3_PWM, R4.Pin_0
  N12: Part1.D4, microSD1.CS
  N13: Part1.D6_PWM, Part2.DO/RX
  N14: Part1.D7, Part2.CK/TX
  N15: Part2.E+, Load_Cell1.wire2
  N16: Part2.E-, Load_Cell1.wire3
  N17: Part2.A+, Load_Cell1.wire1
  N18: Part2.A-, Load_Cell1.wire4
  N19: R4.Pin_1, S3.Pin_3, S3.Pin_4
  N20: U1.Pin_4, U2.COIL2
  N21: R5.Pin_1, LED1.common_cathode
  N22: R6.Pin_0, S4.Pin_1, S4.Pin_2

custom parts:
  RTC_DS1302_module: Arduino module DS1302 SPI Real Time Clock
  Load Cell - Red/white/black/green: A rectangle load cell/weighting pressure Sensor with four wires - Red, white, black, green. Normally corresponding with E+, E-, A+, A- respectively.
  100k0 Ω Resistor: A generic resistor (0.25W)
  Ignition: A generic pushbutton.
  E-Stop: A generic pushbutton.
  12V Battery: Your standard 2x AA battery pack (3 Volts)

// code stored in the sketch: Load_cell_Arduino.ino
//
//    FILE: HX_kitchen_scale.ino
//  AUTHOR: Rob Tillaart
// PURPOSE: HX711 demo
//     URL: https://github.com/RobTillaart/HX711


#include "HX711.h"
#include <SPI.h>
#include "SD.h"

#include <virtuabotixRTC.h>
// Creation of the Real Time Clock Object
virtuabotixRTC myRTC(8, 2, 5);

File Data;
HX711 scale;
int CS =4;

uint8_t dataPin = 6;
uint8_t clockPin = 7;

#define ignition_button 3
#define ignition 9
#define start_countdown_led 10															//RED
#define safe_led	0																					//GREEN
#define e-stop 1
bool ignition_button_status = true;
bool safe = true;


//uint8_t dataPin  = 19;//for esp32
//uint8_t clockPin = 18;//for esp32

void setup()
{
 
  // Set the current date, and time in the following format:
  // seconds, minutes, hours, day of the week, day of the month, month, year
  //myRTC.setDS1302Time(0, 04, 19, 1, 9, 4, 2022);
  Serial.begin(9600);
  Serial.println(__FILE__);
  Serial.print("LIBRARY VERSION: ");
  Serial.println(HX711_LIB_VERSION);
  Serial.println();

  scale.begin(dataPin, clockPin);

  Serial.print("UNITS: ");
  Serial.println(scale.get_units(10));

  Serial.println("\nEmpty the scale, press a key to continue");
  while(!Serial.available());
  while(Serial.available()) Serial.read();

  scale.tare();
  Serial.print("UNITS: ");
  Serial.println(scale.get_units(10));


  Serial.println("\nPut 1000 gram in the scale, press a key to continue");
  while(!Serial.available());
  while(Serial.available()) Serial.read();

  scale.calibrate_scale(1155, 5);
  Serial.print("UNITS: ");
  Serial.println(scale.get_units(10));

  Serial.println("\nScale is calibrated, press a key to continue");
  // Serial.println(scale.get_scale());
  // Serial.println(scale.get_offset());
  while(!Serial.available());
  while(Serial.available()) Serial.read();
  pinMode(10,OUTPUT);
  SD.begin(CS);

//Ignition setup
  Serial.println("The ignition button is ready...");
  pinMode(ignition_button,INPUT_PULLUP);
  pinMode(ignition,OUTPUT);
	pinMode(start_countdown_led,OUTPUT);
	pinMode(safe_led,OUTPUT);
	pinMode(e-stop,INPUT_PULLUP);
	
}


void loop()
{
	ignition_button_status = digitalRead(ignition_button);
	safe = digitalRead(e-stop);
				if(safe == true){
							digitalWrite(safe_led,HIGH);
							break;
							}

  if (ignition_button_status == false && safe == true){
		for(int i=10, i==0, i=--){
				safe = digitalRead(e-stop);
				if(safe == false){
          Serial.print("e-stop was pressed");
				  break;}
				digitalWrite(start_countdown_led,HIGH);
				delay(500);
				digitalWrite(start_countdown_led,LOW);
				delay(500);
		}

	safe = digitalRead(e-stop);
	if(safe == true){
			digitalWrite(start_countdown_led,LOW);
			digitalWrite(safe_led,LOW);
			Serial.print("FIRE!!!");
			digitalWrite(ignition,HIGH);
			}
	
	}

 while(ignition_button_status == true){
    safe = digitalRead(e-stop);
				if(safe == false){
				  Serial.print("e-stop was pressed");
				  break;}
 		myRTC.updateTime();
  	Serial.print("Current Date / Time: ");
 		Serial.print(myRTC.dayofmonth);
 		Serial.print("/");
  	Serial.print(myRTC.month);
  	Serial.print("/");
  	Serial.print(myRTC.year);
  	Serial.print("  ");
  	Serial.print(myRTC.hours);
  	Serial.print(":");
  	Serial.print(myRTC.minutes);
  	Serial.print(":");
  	Serial.print(myRTC.seconds);

  	Serial.print(" UNITS: ");
  	Serial.println(scale.get_units(0.001));

   	Data = SD.open("data.txt", FILE_WRITE);
    if (Data){ 
      Serial.print("Current Date / Time: ");
   		Data.print(myRTC.dayofmonth);
  	 	Data.print("/");
   		Data.print(myRTC.month);
   		Data.print("/");
   		Data.print(myRTC.year);
   		Data.print("  ");
   		Data.print(myRTC.hours);
   		Data.print(":");
   		Data.print(myRTC.minutes);
   		Data.print(":");
   		Data.println(myRTC.seconds);

   		Data.println(scale.get_units(0.001));
   		Data.close();
   		Serial.print("ok ");
    
  }
  else{Serial.print("error ");}
	digitalWrite(ignition,LOW);
 }
}


// -- END OF FILE --
